# Fritzing sketch LCD_Wiring_Matrix_Display (saved by Fritzing 1.0.1rc)
stripboards: 1

parts:
  RPi1 = Raspberry Pi 4B
  GLCD_128x1 = 128 x 64 Graphic LCD
  R6 = TRIMPOT [knob_status=50% package=trimpot_pth_s3_lock]
  S2 = Square Pushbutton
  LED1 = LED - 5mm [color="Red (633nm)" current=0.030 package="5 mm [THT]"]
  Q3 = NPN-Transistor [package="TO92 [THT]"]
  Q4 = PNP-Transistor [package="TO92 [THT]"]
  R7 = Resistor [tolerance=±5% power=0.25 resistance=10k package=THT]
  R8 = Resistor [tolerance=±5% power=0.25 resistance=10k package=THT]
  R9 = Resistor [tolerance=±5% power=0.25 resistance=1.2k package=THT]
  R11 = Resistor [tolerance=±5% power=0.25 resistance=1.2k package=THT]
  JST2 = JST-B4B-XH-A [part_number=B4B-XH-A]
  JST4 = JST-B4B-XH-A [part_number=B4B-XH-A]
  JST3 = JST-B3B-XH-A [part_number=B3B-XH-A]
  JST5 = JST-B4B-XH-A [part_number=B4B-XH-A]
  J1 = JST-B2B-XH-A [part_number=B2B-XH-A]

nets:
  N1: RPi1.GPIO2, GLCD_128x1.4_D/I
  N2: RPi1.5V, GLCD_128x1.2_Vdd, R6.CCW, Q4.E, R8.Pin_1, JST2.connector1, J1.connector0
  N3: RPi1.GPIO3, GLCD_128x1.5_R/W
  N4: RPi1.GND, GLCD_128x1.1_Vss, GLCD_128x1.20_K(-), S2.leg1, LED1.cathode, Q3.E, R7.Pin_0, JST2.connector0, JST4.connector1, JST5.connector1, JST5.connector3, J1.connector1
  N5: RPi1.GPIO4, GLCD_128x1.6_Enable
  N6: RPi1.GPIO14, GLCD_128x1.15_CS1
  N7: RPi1.GPIO15, GLCD_128x1.16_CS2
  N8: RPi1.GPIO17, S2.leg0, JST3.connector0, JST5.connector0
  N9: RPi1.GPIO18, GLCD_128x1.17_RST
  N10: RPi1.GPIO27, LED1.anode, JST3.connector1, JST5.connector2
  N11: RPi1.GPIO22, R9.Pin_1, JST3.connector2
  N12: RPi1.GPIO25, GLCD_128x1.7_DB0
  N13: RPi1.GPIO8, GLCD_128x1.8_DB1
  N14: RPi1.GPIO7, GLCD_128x1.9_BD2
  N15: RPi1.ID_SD, GLCD_128x1.11_DB4
  N16: RPi1.ID_SC, GLCD_128x1.10_DB3
  N17: RPi1.GPIO5, GLCD_128x1.12_DB5
  N18: RPi1.GPIO6, GLCD_128x1.13_DB6
  N19: RPi1.GPIO13, GLCD_128x1.14_DB7
  N20: GLCD_128x1.3_Vo, R6.WIPER, JST2.connector2
  N21: GLCD_128x1.18_Vout, R6.CW, JST2.connector3
  N22: GLCD_128x1.19_A(+), Q4.C, JST4.connector0
  N23: Q3.B, R7.Pin_1, R9.Pin_0
  N24: Q3.C, R8.Pin_0, R11.Pin_0
  N25: Q4.B, R11.Pin_1
